# Fritzing sketch LEDStab (saved by Fritzing 0.9.0b)
breadboards: 1

parts:
  Bauteil2 = Arduino Uno (Rev3)
  R1 = Resistor [tolerance=±5% resistance=100 package=THT]
  R2 = Resistor [tolerance=±5% resistance=100 package=THT]
  LED1 = LED - 5mm [color="Orange (612nm)" package="5 mm [THT]"]
  LED2 = LED - 5mm [color="Orange (612nm)" package="5 mm [THT]"]
  LED3 = LED - 5mm [color="Orange (612nm)" package="5 mm [THT]"]
  R3 = Resistor [tolerance=±5% resistance=100 package=THT]
  R4 = Resistor [tolerance=±5% resistance=100 package=THT]
  LED4 = LED - 5mm [color="Orange (612nm)" package="5 mm [THT]"]
  LED5 = LED - 5mm [color="Orange (612nm)" package="5 mm [THT]"]
  LED6 = LED - 5mm [color="Orange (612nm)" package="5 mm [THT]"]
  R5 = Resistor [tolerance=±5% resistance=100 package=THT]
  R6 = Resistor [tolerance=±5% resistance=100 package=THT]
  LED7 = LED - 5mm [color="Orange (612nm)" package="5 mm [THT]"]
  R7 = Resistor [tolerance=±5% resistance=100 package=THT]
  LED8 = LED - 5mm [color="Orange (612nm)" package="5 mm [THT]"]
  R8 = Resistor [tolerance=±5% resistance=100 package=THT]
  LED9 = LED - 5mm [color="Orange (612nm)" package="5 mm [THT]"]
  R9 = Resistor [tolerance=±5% resistance=100 package=THT]
  LED10 = LED - 5mm [color="Orange (612nm)" package="5 mm [THT]"]
  R10 = Resistor [tolerance=±5% resistance=100 package=THT]
  LED11 = LED - 5mm [color="Orange (612nm)" package="5 mm [THT]"]
  R11 = Resistor [tolerance=±5% resistance=100 package=THT]
  LED12 = LED - 5mm [color="Orange (612nm)" package="5 mm [THT]"]
  R12 = Resistor [tolerance=±5% resistance=100 package=THT]
  LED13 = LED - 5mm [color="Orange (612nm)" package="5 mm [THT]"]
  R13 = Resistor [tolerance=±5% resistance=100 package=THT]
  LED14 = LED - 5mm [color="Orange (612nm)" package="5 mm [THT]"]
  LED15 = LED - 5mm [color="Orange (612nm)" package="5 mm [THT]"]
  LED16 = LED - 5mm [color="Orange (612nm)" package="5 mm [THT]"]
  LED17 = LED - 5mm [color="Orange (612nm)" package="5 mm [THT]"]
  LED18 = LED - 5mm [color="Orange (612nm)" package="5 mm [THT]"]
  R14 = Resistor [tolerance=±5% resistance=100 package=THT]
  R15 = Resistor [tolerance=±5% resistance=100 package=THT]
  R16 = Resistor [tolerance=±5% resistance=100 package=THT]
  R17 = Resistor [tolerance=±5% resistance=100 package=THT]
  R18 = Resistor [tolerance=±5% resistance=100 package=THT]
  Poti = Rotary Potentiometer (Small) [maximum_resistance=100kΩ package=THT]
  Button = Pushbutton [package="[THT]"]
  9V_Batterie = Battery block 9V
  Wippschalter = Toggle Switch [package=THT]
  R20 = Resistor [tolerance=±5% resistance=100 package=THT]

nets:
  N1: Bauteil2.A0, Poti.wiper
  N2: Bauteil2.A1, LED18.cathode
  N3: Bauteil2.A2, LED17.cathode
  N4: Bauteil2.A3, LED16.cathode
  N5: Bauteil2.A4/SDA, LED15.cathode
  N6: Bauteil2.A5/SCL, LED14.cathode
  N7: Bauteil2.D8, LED5.cathode
  N8: Bauteil2.D9_PWM, LED4.cathode
  N9: Bauteil2.D10_PWM/SS, LED3.cathode
  N10: Bauteil2.D11_PWM/MOSI, LED2.cathode
  N11: Bauteil2.D12/MISO, LED1.cathode
  N12: Bauteil2.D13/SCK, Button.Pin_3, Button.Pin_4, R20.Pin_0
  N13: Bauteil2.D0/RX, LED13.cathode
  N14: Bauteil2.D1/TX, LED12.cathode
  N15: Bauteil2.D2, LED11.cathode
  N16: Bauteil2.D3_PWM, LED10.cathode
  N17: Bauteil2.D4, LED9.cathode
  N18: Bauteil2.D5_PWM, LED8.cathode
  N19: Bauteil2.D6_PWM, LED7.cathode
  N20: Bauteil2.D7, LED6.cathode
  N21: Bauteil2.3V3, Poti.leg1
  N22: Bauteil2.5V, Button.Pin_1, Button.Pin_2
  N23: Bauteil2.GND, R1.Pin_1, R2.Pin_1, R3.Pin_1, R4.Pin_1, R5.Pin_1, R6.Pin_1, R7.Pin_1, R8.Pin_1, R9.Pin_1, R10.Pin_1, R11.Pin_1, R12.Pin_1, R13.Pin_1, R14.Pin_1, R15.Pin_1, R16.Pin_1, R17.Pin_1, R18.Pin_1, Poti.leg2, 9V_Batterie.-, R20.Pin_1
  N24: Bauteil2.VIN, Wippschalter.L1
  N25: R1.Pin_0, LED1.anode
  N26: R2.Pin_0, LED2.anode
  N27: LED3.anode, R3.Pin_0
  N28: R4.Pin_0, LED4.anode
  N29: LED5.anode, R5.Pin_0
  N30: LED6.anode, R6.Pin_0
  N31: LED7.anode, R7.Pin_0
  N32: LED8.anode, R8.Pin_0
  N33: LED9.anode, R9.Pin_0
  N34: LED10.anode, R10.Pin_0
  N35: LED11.anode, R11.Pin_0
  N36: LED12.anode, R12.Pin_0
  N37: LED13.anode, R13.Pin_0
  N38: LED14.anode, R14.Pin_0
  N39: LED15.anode, R15.Pin_0
  N40: LED16.anode, R16.Pin_0
  N41: LED17.anode, R17.Pin_0
  N42: LED18.anode, R18.Pin_0
  N43: 9V_Batterie.+, Wippschalter.L2

notes:
  oben
  unten
  9V Batterie
